# Fritzing sketch WiringDiagram (saved by Fritzing 1.0.4)
stripboards: 2
breadboards: 1

parts:
  A3 = Arduino Nano ESP32
  S18 = Pushbutton [package="[THT]"]
  LED13 = LED - 5mm [color="Orange (605nm)" current=0.030A package="5 mm [THT]"]
  R51 = Rotary Potentiometer (Small) [maximum_resistance=10kΩ knob_status=50% power=0.5W package=THT]
  M7 = DC Motor [voltage_(max)=3.3V voltage_(min)=3V]
  M8 = DC Motor [voltage_(max)=6V voltage_(min)=3V]
  J6 = Piezo Speaker
  meter2 = meter
  U5 = mystery part, 3 pins [chip_label=HE]
  R54 = Resistor [tolerance=±5% power=0.25W resistance=10 package=THT]
  C6 = Electrolytic Capacitor [capacitance=0.1mF voltage=35V package="100 mil [THT, electrolytic]"]
  R56 = Resistor [tolerance=±5% power=0.25W resistance=22 package=THT]
  J7 = Basic Servo
  R58 = Resistor [tolerance=±5% power=0.25W resistance=1k package=THT]
  R59 = Resistor [tolerance=±5% power=0.25W resistance=220 package=THT]
  S19 = Pushbutton [package="[THT]"]
  S20 = Pushbutton [package="[THT]"]
  S21 = Pushbutton [package="[THT]"]
  S22 = Pushbutton [package="[THT]"]
  S23 = Pushbutton [package="[THT]"]
  S24 = Pushbutton [package="[THT]"]
  R62 = Resistor [tolerance=±5% power=0.25W resistance=1k package=THT]
  R63 = Resistor [tolerance=±5% power=0.25W resistance=1k package=THT]
  R64 = Resistor [tolerance=±5% power=0.25W resistance=1k package=THT]
  R65 = Resistor [tolerance=±5% power=0.25W resistance=1k package=THT]
  R66 = Resistor [tolerance=±5% power=0.25W resistance=1k package=THT]
  M9 = Stepper Motor - Bipolar  # not connected
  Q6 = Basic FET P-Channel [package="TO220 [THT]"]
  R72 = Resistor [tolerance=±5% power=0.25W resistance=1k package=THT]
  R73 = Resistor [tolerance=±5% power=0.25W resistance=1k package=THT]
  R74 = Resistor [tolerance=±5% power=0.25W resistance=10k package=THT]
  R76 = Resistor [tolerance=±5% power=0.25W resistance=470 package=THT]
  LED17 = LED - 5mm [color="Red (633nm)" current=0.030A package="5 mm [THT]"]
  R77 = Resistor [tolerance=±5% power=0.25W resistance=1k package=THT]
  Q7 = Basic FET P-Channel [package="TO220 [THT]"]
  R78 = Resistor [tolerance=±5% power=0.25W resistance=2.2k package=THT]
  R79 = Resistor [tolerance=±5% power=0.25W resistance=2.2k package=THT]
  R80 = Resistor [tolerance=±5% power=0.25W resistance=220 package=THT]
  S17 = Toggle Switch [package=THT]
  LED18 = LED - 5mm [color="Orange (605nm)" current=0.030A package="5 mm [THT]"]
  LED19 = LED - 5mm [color="Orange (605nm)" current=0.030A package="5 mm [THT]"]
  R81 = Slide Potentiometer [maximum_resistance=10kΩ knob_status=50% power=0.5W package=THT]

nets:
  N1: A3.Pin_1, meter2.Positive
  N2: A3.Pin_2, S18.Pin_3, S18.Pin_4, R51.leg2, U5.pin1, R54.Pin_0, R56.Pin_0, R74.Pin_0, R77.Pin_0, S17.L1
  N3: A3.Pin_4, R58.Pin_1, S19.Pin_1, S19.Pin_2, S20.Pin_1, S20.Pin_2, S21.Pin_1, S21.Pin_2, S22.Pin_1, S22.Pin_2, S23.Pin_1, S23.Pin_2, S24.Pin_1, S24.Pin_2
  N4: A3.Pin_5, S18.Pin_1, S18.Pin_2, R73.Pin_1
  N5: A3.Pin_6, R81.leg1
  N6: A3.Pin_8, R72.Pin_1, S17.COM
  N7: A3.Pin_9, R51.wiper, R76.Pin_0, LED18.anode
  N8: A3.Pin_10, U5.pin3, R74.Pin_1
  N9: A3.Pin_11, R80.Pin_1
  N10: A3.Pin_12, C6.+, J7.vcc
  N11: A3.Pin_14, A3.Pin_19, LED13.cathode, J6.pin1, meter2.Com, U5.pin2, C6.-, J7.gnd, R58.Pin_0, Q6.source, R72.Pin_0, R73.Pin_0, LED17.cathode, Q7.source, LED18.cathode, LED19.cathode
  N12: A3.Pin_20, R79.Pin_1
  N13: A3.Pin_21, J7.pulse
  N14: A3.Pin_24, R59.Pin_1
  N15: A3.Pin_26, R78.Pin_0
  N16: LED13.anode, R59.Pin_0
  N17: M7.pin_1, Q6.drain
  N18: M7.pin_2, R54.Pin_1
  N19: M8.pin_1, R56.Pin_1
  N20: M8.pin_2, Q7.drain
  N21: J6.pin2, R81.wiper
  N22: S19.Pin_3, S19.Pin_4, R62.Pin_0, R63.Pin_1
  N23: S20.Pin_3, S20.Pin_4, R63.Pin_0, R64.Pin_1
  N24: S21.Pin_3, S21.Pin_4, R64.Pin_0, R65.Pin_1
  N25: S22.Pin_3, S22.Pin_4, R65.Pin_0, R66.Pin_1
  N26: S23.Pin_3, S23.Pin_4, R66.Pin_0, R77.Pin_1
  N27: S24.Pin_3, S24.Pin_4
  N28: Q6.gate, R79.Pin_0
  N29: R76.Pin_1, LED19.anode
  N30: LED17.anode, R80.Pin_0
  N31: Q7.gate, R78.Pin_1

custom parts:
  Arduino Nano ESP32: Arduino® Nano ESP32 tht.
  meter: A generic analog meter.
